# Fritzing sketch Flipper GPIO to 10-Pin SWD Breakout (saved by Fritzing 1.0.3b)
circuit board: 6.36026cm x 2.28004cm
breadboards: 1

parts:
  Flipper_GPIO = Flipper Zero GPIO Male pins [form="♂ (male)" package=THT]
  SWD2 = male pin header, 5 pins [form="♂ (male)"]
  SWD1 = male pin header, 5 pins [form="♂ (male)"]

nets:
  GND: Flipper_GPIO.pin8, Flipper_GPIO.pin11, Flipper_GPIO.pin18, SWD1.pin2, SWD1.pin3, SWD1.pin5
  N1: Flipper_GPIO.pin9, SWD1.pin1
  N2: Flipper_GPIO.pin10, SWD2.pin2
  N3: Flipper_GPIO.pin12, SWD2.pin1

custom parts:
  Flipper Zero GPIO Male pins: Flipper Zero GPIO as 2.54mm male header pins
